# Fritzing sketch led tester v2-ORG (saved by Fritzing 0.8.3b)
circuit board: 4.98828cm x 3.69711cm
breadboards: 1

parts:
  CR2032_(20mm_SMD) = Battery Holders [package=battcon_20mm]
  - = Pad [width=7.38481481481481 height=19.3087225185185 connect=center]
  + = Pad [width=6.20887948148148 height=6.77334274074074 connect=center]
  68_ohm_0805 = Resistor [tolerance=±5% resistance=68 package="0805 [SMD]"]
  6x6x5mm_4_Pins_SMD_Tact_Switche = Pushbutton [package="[SMD]"]
  LED1_0805 = smd LED [color="Blue (525nm)" package="0805 [SMD]"]
  68_ohm1_0805 = Resistor [tolerance=±5% resistance=68 package="0805 [SMD]"]
  5mm = LED - 5mm [color="Red (633nm)" package="5 mm [THT]"]
  0603 = smd LED [color="Red (633nm)" package="0603 [SMD]"]
  0805 = smd LED [color="Red (633nm)" package="0805 [SMD]"]
  1206 = smd LED [color="Red (633nm)" package="1206 [SMD]"]
  Pad2 = Pad [width=2.18722222222222 height=4.30388888888889 connect=center]
  Pad3 = Pad [width=2.18722222222222 height=4.30388888888889 connect=center]

nets:
  N1: CR2032_(20mm_SMD).+, +.pad
  GND: CR2032_(20mm_SMD).-, -.pad, LED1_0805.cathode, 5mm.cathode, 0603.anode, 0805.anode, 1206.anode_-, Pad3.pad
  N2: 68_ohm_0805.Pin_0, 6x6x5mm_4_Pins_SMD_Tact_Switche.Pin_3, 6x6x5mm_4_Pins_SMD_Tact_Switche.Pin_4
  N3: 68_ohm_0805.Pin_1, LED1_0805.anode
  N4: 6x6x5mm_4_Pins_SMD_Tact_Switche.Pin_1, 6x6x5mm_4_Pins_SMD_Tact_Switche.Pin_2, 68_ohm1_0805.Pin_0
  N5: 68_ohm1_0805.Pin_1, 5mm.anode, 0603.cathode, 0805.cathode, 1206.cathode_+, Pad2.pad

notes:
  --------------------
  +
  -
  20mm
  CR2032
  BATT
  TEST
  LED
  LED TESTER
  20/01/2014
  3V

custom parts:
  Red LED - 5mm: A generic red LED (~1.8V)
  Blue smd LED: A generic blue LED (~1.8V)
