# Fritzing sketch led tester v2 (saved by Fritzing 0.9.2b)
breadboards: 1

parts:
  68_ohm_0805 = Resistor [tolerance=±5% resistance=68 package="0805 [SMD]"]
  LED1_0805 = smd LED [color="Blue (525nm)" package="0805 [SMD]"]
  68_ohm1_0805 = Resistor [tolerance=±5% resistance=68 package="0805 [SMD]"]
  5mm = LED - 5mm [color="Red (633nm)" package="5 mm [THT]"]
  0603 = smd LED [color="Red (633nm)" package="0603 [SMD]"]
  0805 = smd LED [color="Red (633nm)" package="0805 [SMD]"]
  1206 = smd LED [color="Red (633nm)" package="1206 [SMD]"]
  part = Blue smd LED [package="1206 [SMD]"]  # not connected
  6x6x5mm_4_Pins_SMD_Tact_Switche = Pushbutton [package="[THT]"]
  CR2032_(20mm_SMD) = Battery Holders [package=battcon_12mm]

nets:
  N1: 68_ohm_0805.Pin_0, 6x6x5mm_4_Pins_SMD_Tact_Switche.Pin_3, 6x6x5mm_4_Pins_SMD_Tact_Switche.Pin_4
  N2: 68_ohm_0805.Pin_1, LED1_0805.anode
  GND: LED1_0805.cathode, 5mm.cathode, 0603.anode, 0805.anode, 1206.anode_-, CR2032_(20mm_SMD).-
  N3: 68_ohm1_0805.Pin_0, 6x6x5mm_4_Pins_SMD_Tact_Switche.Pin_1, 6x6x5mm_4_Pins_SMD_Tact_Switche.Pin_2, CR2032_(20mm_SMD).+
  N4: 68_ohm1_0805.Pin_1, 5mm.anode, 0603.cathode, 0805.cathode, 1206.cathode_+

notes:
  --------------------
  ----------
  20mm
  CR2032
  BATT
  TEST
  LED
  LED TESTER
  20/01/2014
  3V
  +
  -

custom parts:
  Red LED - 5mm: A generic red LED (~1.8V)
  Blue smd LED: A generic blue LED (~1.8V)
